# Fritzing sketch abaqs-fritzing (saved by Fritzing 0.9.1b)
circuit board: 8.46667cm x 5.64444cm

parts:
  RHT1 = Humidity and Temperature Sensor RHT03
  Part4 = Arduino Prototyping Shield
  Part5 = Bluetooth Mate Silver
  JP1 = Header 6 [package=em406]  # not connected
  JP4 = Header 6 [package=molex-1x6-ra]
  R1 = Resistor [tolerance=±5% resistance=150 package=THT]
  JP5 = Header 4 [package=1x04-smd]
  C1 = Electrolytic Capacitor [capacitance=0.22mF package="100 mil [THT, electrolytic]"]
  R2 = Resistor [tolerance=±5% resistance=1k package=THT]

nets:
  VCC: RHT1.Vcc, Part4.+5V, Part4.N$45, Part4.N$363, Part4.N$427, JP4.6, R1.Pin_1, C1.+, R2.Pin_0
  N1: RHT1.Data-signal, Part4.D5, Part4.N$430, R2.Pin_1
  N2: RHT1.GND_2, Part4.GND, Part4.N$292, Part4.N$321, Part4.N$324, JP4.2, JP4.4, C1.-
  N3: Part4.D4, Part4.N$418, Part4.N$419, Part5.RX_5V, JP5.4
  N4: Part4.D2, Part4.N$322, JP4.3
  N5: Part4.D3, Part4.N$414, Part4.N$415, Part5.TX_5V, JP5.3
  N6: Part4.A0, Part4.N$325, JP4.5
  N7: Part4.N$105, JP4.1, R1.Pin_0
  N8: Part4.N$240, Part4.N$307, Part5.CTS_5V, JP5.1
  N9: Part4.N$241, Part4.N$313, Part5.VCC, JP5.2
  N10: Part4.N$268, Part5.GND
  N11: Part4.N$435, Part5.RTS_5V
