# Fritzing sketch abaqs2 (saved by Fritzing 0.9.1b)
circuit board: 8.1968cm x 5.21464cm

parts:
  JP1 = Header 3 [package=molex-1x3_lock]
  R1 = Resistor [tolerance=±5% resistance=1k package=THT]
  R3 = Resistor [tolerance=±5% resistance=150 package=THT]
  C1 = Electrolytic Capacitor [capacitance=0.22mF voltage=16V package="100 mil [THT, electrolytic]"]
  JP4 = Header 4 [package=molex-1x4_lock]
  JP5 = Header 6 [package=molex-1x6_lock]
  Part1 = Arduino Prototyping Shield
  RHT1 = Humidity and Temperature Sensor RHT03
  FAN = DC Motor
  JP8 = Header 4 [package=molex-1x4_lock]
  R2 = Resistor [tolerance=±5% resistance=1k package=THT]
  D1 = Rectifier Diode [part_number=1N4001 package="300 mil [THT]"]
  R4 = Resistor [tolerance=±5% resistance=1k package=THT]
  Q1 = NPN-Transistor [package="SOT-23 [SMD]"]
  R5 = Resistor [tolerance=±5% resistance=220 package=THT]
  R6 = Resistor [tolerance=±5% resistance=220 package=THT]
  R7 = Resistor [tolerance=±5% resistance=220 package=THT]
  LED1 = LED - 5mm [color="Red (633nm)" package="5 mm [THT]"]
  LED2 = LED - 5mm [color="Yellow (585nm)" package="5 mm [THT]"]
  LED3 = LED - 5mm [color="Green (565nm)" package="5 mm [THT]"]

nets:
  N1: JP1.1, Part1.N$261, Part1.N$262, Part1.N$298, Part1.N$315, FAN.pin_1, D1.cathode, Q1.1
  N2: JP1.2, Part1.+9V, Part1.N$297, FAN.pin_2
  N3: JP1.3, Part1.D6, Part1.N$299, Part1.N$419, R4.Pin_1
  N4: R1.Pin_0, Part1.N$235, Part1.N$259, Q1.0
  N5: R1.Pin_1, Part1.D13, Part1.N$245
  +5V: R3.Pin_0, JP4.4, JP5.6, Part1.+5V, Part1.N$283, Part1.N$289, Part1.N$360, Part1.N$385, Part1.N$423, RHT1.Vcc, JP8.4, R2.Pin_1, R4.Pin_0
  N6: R3.Pin_1, C1.+, JP5.1, Part1.N$353, Part1.N$358
  GND: C1.-, JP4.3, JP5.2, JP5.4, Part1.GND, Part1.N$46, Part1.N$47, Part1.N$272, Part1.N$322, Part1.N$323, Part1.N$325, Part1.N$326, Part1.N$362, Part1.N$407, RHT1.GND_1, RHT1.GND_2, JP8.1, JP8.2, D1.anode, Q1.2, LED1.cathode, LED2.cathode, LED3.cathode
  N7: JP4.1, Part1.D3, Part1.N$153
  N8: JP4.2, Part1.D4, Part1.N$408
  N9: JP5.3, Part1.D2, Part1.N$368
  N10: JP5.5, Part1.A0, Part1.N$93
  N11: Part1.D5, Part1.N$70, Part1.N$286, RHT1.Data-signal, JP8.3, R2.Pin_0
  N12: Part1.D9, Part1.N$106, R7.Pin_1
  N13: Part1.D10, Part1.N$131, R6.Pin_1
  N14: Part1.D11, Part1.N$155, R5.Pin_1
  N15: Part1.N$72, Part1.N$73, R7.Pin_0, LED3.anode
  N16: Part1.N$77, R6.Pin_0, LED2.anode
  N17: Part1.N$118, R5.Pin_0, LED1.anode

custom parts:
  Header 6: Header 6 Standard 6-pin 0.1 header. Use with straight break away headers (SKU : PRT-00116), right angle break away headers (PRT-00553), swiss pins (PRT-00743), machine pins (PRT-00117), and female headers (PRT-00115). Molex polarized connector foot print use with SKU : PRT-08094 with associated crimp pins and housings. NOTES ON THE VARIANTS LOCK and LOCK_LONGPADS... This footprint was designed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
